# Fritzing sketch Stepper Driver Board (saved by Fritzing 0.9.3b)
circuit board: 9.98119cm x 10cm

parts:
  DRV_1 = DRV 8825 Stepper Motor Carrier, High Current [part_number="DRV 8825"]
  Arduino_Mega = double row female pin header, 38 pins [form="♀ (female)"]
  DRV_2 = DRV 8825 Stepper Motor Carrier, High Current [part_number="DRV 8825"]
  DRV_3 = DRV 8825 Stepper Motor Carrier, High Current [part_number="DRV 8825"]
  DRV_4 = DRV 8825 Stepper Motor Carrier, High Current [part_number="DRV 8825"]
  DRV_5 = DRV 8825 Stepper Motor Carrier, High Current [part_number="DRV 8825"]
  DRV_6 = DRV 8825 Stepper Motor Carrier, High Current [part_number="DRV 8825"]
  DRV_7 = DRV 8825 Stepper Motor Carrier, High Current [part_number="DRV 8825"]
  DRV_8 = DRV 8825 Stepper Motor Carrier, High Current [part_number="DRV 8825"]
  DRV_9 = DRV 8825 Stepper Motor Carrier, High Current [part_number="DRV 8825"]
  Fan_1 = Pad [width=10 height=40 connect=center]  # not connected
  Fan_2 = Pad [width=10 height=40 connect=center]  # not connected
  STP1 = female pin header, 4 pins [form="♀ (female)"]
  STP2 = female pin header, 4 pins [form="♀ (female)"]
  STP3 = female pin header, 4 pins [form="♀ (female)"]
  STP4 = female pin header, 4 pins [form="♀ (female)"]
  STP5 = female pin header, 4 pins [form="♀ (female)"]
  STP6 = female pin header, 4 pins [form="♀ (female)"]
  STP7 = female pin header, 4 pins [form="♀ (female)"]
  STP8 = female pin header, 4 pins [form="♀ (female)"]
  STP9 = female pin header, 4 pins [form="♀ (female)"]
  +FAN- = female pin header, 2 pins [form="♀ (female)"]
  +FAN-_2 = female pin header, 2 pins [form="♀ (female)"]
  +12- = female pin header, 2 pins [form="♀ (female)"]
  +5- = female pin header, 2 pins [form="♀ (female)"]
  C1 = Electrolytic Capacitor [capacitance=1mF voltage=20V package="200 mil [THT, electrolytic]"]
  C2 = Electrolytic Capacitor [capacitance=1mF voltage=20V package="200 mil [THT, electrolytic]"]
  C3 = Electrolytic Capacitor [capacitance=1mF voltage=20V package="200 mil [THT, electrolytic]"]
  +12-_2 = female pin header, 2 pins [form="♀ (female)"]
  +12-_3 = female pin header, 2 pins [form="♀ (female)"]

nets:
  N1: DRV_1.ENABLE, Arduino_Mega.pin22
  N2: DRV_1.RESET, DRV_1.SLEEP, Arduino_Mega.pin1, DRV_2.RESET, DRV_2.SLEEP, DRV_3.RESET, DRV_3.SLEEP, DRV_4.RESET, DRV_4.SLEEP, DRV_5.RESET, DRV_5.SLEEP, DRV_6.RESET, DRV_6.SLEEP, DRV_7.RESET, DRV_7.SLEEP, DRV_8.RESET, DRV_8.SLEEP, DRV_9.RESET, DRV_9.SLEEP, +5-.pin2
  N3: DRV_1.STEP, Arduino_Mega.pin23
  N4: DRV_1.DIRECTION, Arduino_Mega.pin24
  N5: DRV_1.VOLTAGE_ST/_MT, DRV_4.VOLTAGE_ST/_MT, DRV_7.VOLTAGE_ST/_MT, +12-.pin2, C1.+
  N6: DRV_1.GROUND_ST/_MT, DRV_4.GROUND_ST/_MT, DRV_7.GROUND_ST/_MT, +12-.pin1, C1.-
  N7: DRV_1.OUT_2B, STP1.pin1
  N8: DRV_1.OUT_2A, STP1.pin2
  N9: DRV_1.OUT_1A, STP1.pin3
  N10: DRV_1.OUT_1B, STP1.pin4
  N11: DRV_1.GROUND_LOG, Arduino_Mega.pin19, DRV_2.GROUND_LOG, DRV_3.GROUND_LOG, DRV_4.GROUND_LOG, DRV_5.GROUND_LOG, DRV_6.GROUND_LOG, DRV_7.GROUND_LOG, DRV_8.GROUND_LOG, DRV_9.GROUND_LOG, +5-.pin1
  N12: Arduino_Mega.pin2, DRV_9.DIRECTION
  N13: Arduino_Mega.pin3, DRV_9.STEP
  N14: Arduino_Mega.pin4, DRV_9.ENABLE
  N15: Arduino_Mega.pin5, DRV_6.DIRECTION
  N16: Arduino_Mega.pin6, DRV_6.STEP
  N17: Arduino_Mega.pin7, DRV_6.ENABLE
  N18: Arduino_Mega.pin8, DRV_3.DIRECTION
  N19: Arduino_Mega.pin9, DRV_3.STEP
  N20: Arduino_Mega.pin10, DRV_3.ENABLE
  N21: Arduino_Mega.pin11, DRV_8.DIRECTION
  N22: Arduino_Mega.pin12, DRV_8.STEP
  N23: Arduino_Mega.pin13, DRV_8.ENABLE
  N24: Arduino_Mega.pin14, DRV_5.DIRECTION
  N25: Arduino_Mega.pin15, DRV_5.STEP
  N26: Arduino_Mega.pin16, DRV_5.ENABLE
  N27: Arduino_Mega.pin17, DRV_2.DIRECTION
  N28: Arduino_Mega.pin18, DRV_2.STEP
  N29: Arduino_Mega.pin21, DRV_2.ENABLE
  N30: Arduino_Mega.pin25, DRV_4.ENABLE
  N31: Arduino_Mega.pin26, DRV_4.STEP
  N32: Arduino_Mega.pin27, DRV_4.DIRECTION
  N33: Arduino_Mega.pin28, DRV_7.ENABLE
  N34: Arduino_Mega.pin29, DRV_7.STEP
  N35: Arduino_Mega.pin30, DRV_7.DIRECTION
  N36: DRV_2.VOLTAGE_ST/_MT, DRV_5.VOLTAGE_ST/_MT, DRV_8.VOLTAGE_ST/_MT, C2.+, +12-_2.pin2
  N37: DRV_2.GROUND_ST/_MT, DRV_5.GROUND_ST/_MT, DRV_8.GROUND_ST/_MT, C2.-, +12-_2.pin1
  N38: DRV_2.OUT_2B, STP2.pin1
  N39: DRV_2.OUT_2A, STP2.pin2
  N40: DRV_2.OUT_1A, STP2.pin3
  N41: DRV_2.OUT_1B, STP2.pin4
  N42: DRV_3.VOLTAGE_ST/_MT, DRV_6.VOLTAGE_ST/_MT, DRV_9.VOLTAGE_ST/_MT, +FAN-.pin2, +FAN-_2.pin2, C3.+, +12-_3.pin2
  N43: DRV_3.GROUND_ST/_MT, DRV_6.GROUND_ST/_MT, DRV_9.GROUND_ST/_MT, +FAN-.pin1, +FAN-_2.pin1, C3.-, +12-_3.pin1
  N44: DRV_3.OUT_2B, STP3.pin1
  N45: DRV_3.OUT_2A, STP3.pin2
  N46: DRV_3.OUT_1A, STP3.pin3
  N47: DRV_3.OUT_1B, STP3.pin4
  N48: DRV_4.OUT_2B, STP4.pin1
  N49: DRV_4.OUT_2A, STP4.pin2
  N50: DRV_4.OUT_1A, STP4.pin3
  N51: DRV_4.OUT_1B, STP4.pin4
  N52: DRV_5.OUT_2B, STP5.pin1
  N53: DRV_5.OUT_2A, STP5.pin2
  N54: DRV_5.OUT_1A, STP5.pin3
  N55: DRV_5.OUT_1B, STP5.pin4
  N56: DRV_6.OUT_2B, STP6.pin1
  N57: DRV_6.OUT_2A, STP6.pin2
  N58: DRV_6.OUT_1A, STP6.pin3
  N59: DRV_6.OUT_1B, STP6.pin4
  N60: DRV_7.OUT_2B, STP7.pin1
  N61: DRV_7.OUT_2A, STP7.pin2
  N62: DRV_7.OUT_1A, STP7.pin3
  N63: DRV_7.OUT_1B, STP7.pin4
  N64: DRV_8.OUT_2B, STP8.pin1
  N65: DRV_8.OUT_2A, STP8.pin2
  N66: DRV_8.OUT_1A, STP8.pin3
  N67: DRV_8.OUT_1B, STP8.pin4
  N68: DRV_9.OUT_2B, STP9.pin1
  N69: DRV_9.OUT_2A, STP9.pin2
  N70: DRV_9.OUT_1A, STP9.pin3
  N71: DRV_9.OUT_1B, STP9.pin4

notes:
  Stepper Driver Board 1.0
  Event Horizon
